// Logisim project bfcpu.circ as structural Verilog: 5 circuits, main circuit Register4
module main (
  input  RESET
);

  wire CLC, OE, WE;
  wire [1:0] DPREG, DREG, IPREG, SPREG;
  wire [7:0] D_d_out, IP_d_out, RAM1_dout, RAM2_dout;
  wire [15:0] DP_d_out;

  RegisterDriver registerdriver_1 ();  // open: RS0, RS1, RS2, CE, DEC, CLC, R0, R1, R2, R3, R4, R5, R6, R7
  Register8 I ();  // open: RESET, EN, LD, UP, DN, D_IN, D_OUT
  Register4 F ();  // open: EN, LD, UP, DN, D_IN, RESET, D_OUT
  Register8 LS ();  // open: RESET, EN, LD, UP, DN, D_IN, D_OUT
  RAM #(.addrWidth(16)) RAM1 (.addr(DP_d_out), .we(WE), .oe(OE), .clk(CLC), .din(D_d_out), .dout(RAM1_dout));
  Register8 D (.RESET(RESET), .UP(DREG[0]), .DN(DREG[1]), .D_IN(RAM1_dout), .D_OUT(D_d_out));  // open: EN, LD
  Register16 DP (.D_IN(16'h6), .LD(RESET), .UP(DPREG[0]), .DN(DPREG[1]), .D_OUT(DP_d_out));  // open: RESET, EN
  Register16 SP (.RESET(RESET), .UP(SPREG[0]), .DN(SPREG[1]), .D_OUT(DP_d_out));  // open: D_IN, EN, LD
  RAM #(.addrWidth(16)) RAM2 (.addr(DP_d_out), .we(WE), .oe(OE), .clk(CLC), .din(IP_d_out), .dout(RAM2_dout));
  Register16 IP (
    .D_IN({RAM1_dout, RAM2_dout}), .RESET(RESET), .UP(IPREG[0]), .DN(IPREG[1]), .D_OUT({IP_d_out, D_d_out}));  // open: EN, LD

  // Other names for the same wires on the sheet: R = RESET

  // Notes on the sheet:
  //   RESET VECTOR
endmodule

module Register4 (
  input  EN,
  input  LD,
  input  UP,
  input  DN,
  input  [3:0] D_IN,
  input  RESET,
  output [3:0] D_OUT
);

  wire n74193_1_pin11;
  wire [3:0] n74193_1_pin3;

  _74193 u_74193_1 (
    .pin1(D_IN[1]), .pin2(n74193_1_pin3[1]), .pin3(n74193_1_pin3[0]), .pin4(DN), .pin5(UP),
    .pin6(n74193_1_pin3[2]), .pin7(n74193_1_pin3[3]), .pin15(D_IN[0]), .pin14(RESET), .pin11(n74193_1_pin11),
    .pin10(D_IN[2]), .pin9(D_IN[3]));  // open: pin13, pin12
  not not_1 (n74193_1_pin11, LD);
  Hex_Digit_Display hex_digit_display_1 (.value(n74193_1_pin3));  // open: dp
  assign D_OUT = EN ? n74193_1_pin3 : 4'bz;  // Controlled_Buffer controlled_buffer_1
endmodule

module Register8 (
  input  [7:0] D_IN,
  input  EN,
  input  LD,
  input  UP,
  input  DN,
  input  RESET,
  output [7:0] D_OUT
);

  wire n74193_1_pin11, n74193_1_pin12, n74193_1_pin13, n74193_2_pin11;
  wire [3:0] n74193_1_pin3, n74193_2_pin3;

  _74193 u_74193_1 (
    .pin1(D_IN[1]), .pin2(n74193_1_pin3[1]), .pin3(n74193_1_pin3[0]), .pin4(DN), .pin5(UP),
    .pin6(n74193_1_pin3[2]), .pin7(n74193_1_pin3[3]), .pin15(D_IN[0]), .pin14(RESET), .pin13(n74193_1_pin13),
    .pin12(n74193_1_pin12), .pin11(n74193_1_pin11), .pin10(D_IN[2]), .pin9(D_IN[3]));
  not not_1 (n74193_1_pin11, LD);
  Hex_Digit_Display hex_digit_display_1 (.value(n74193_1_pin3));  // open: dp
  assign D_OUT[7:4] = EN ? n74193_1_pin3 : 4'bz;  // Controlled_Buffer controlled_buffer_1
  _74193 u_74193_2 (
    .pin1(D_IN[5]), .pin2(n74193_2_pin3[1]), .pin3(n74193_2_pin3[0]), .pin4(n74193_1_pin13),
    .pin5(n74193_1_pin12), .pin6(n74193_2_pin3[2]), .pin7(n74193_2_pin3[3]), .pin15(D_IN[4]), .pin14(RESET),
    .pin11(n74193_2_pin11), .pin10(D_IN[6]), .pin9(D_IN[7]));  // open: pin13, pin12
  not not_2 (n74193_2_pin11, LD);
  Hex_Digit_Display hex_digit_display_2 (.value(n74193_2_pin3));  // open: dp
  assign D_OUT[3:0] = EN ? n74193_2_pin3 : 4'bz;  // Controlled_Buffer controlled_buffer_2

  // Other names for the same wires on the sheet: R = RESET
endmodule

module Register16 (
  input  [15:0] D_IN,
  input  EN,
  input  LD,
  input  UP,
  input  DN,
  input  RESET,
  output [15:0] D_OUT
);

  wire n74193_1_pin11, n74193_1_pin12, n74193_1_pin13, n74193_2_pin11, n74193_2_pin12, n74193_2_pin13,
       n74193_3_pin11, n74193_3_pin12, n74193_3_pin13, n74193_4_pin11;
  wire [3:0] n74193_1_pin3, n74193_2_pin3, n74193_3_pin3, n74193_4_pin3;

  _74193 u_74193_1 (
    .pin1(D_IN[1]), .pin2(n74193_1_pin3[1]), .pin3(n74193_1_pin3[0]), .pin4(DN), .pin5(UP),
    .pin6(n74193_1_pin3[2]), .pin7(n74193_1_pin3[3]), .pin15(D_IN[0]), .pin14(RESET), .pin13(n74193_1_pin13),
    .pin12(n74193_1_pin12), .pin11(n74193_1_pin11), .pin10(D_IN[2]), .pin9(D_IN[3]));
  not not_1 (n74193_1_pin11, LD);
  Hex_Digit_Display hex_digit_display_1 (.value(n74193_1_pin3));  // open: dp
  assign D_OUT[3:0] = EN ? n74193_1_pin3 : 4'bz;  // Controlled_Buffer controlled_buffer_1
  _74193 u_74193_2 (
    .pin1(D_IN[5]), .pin2(n74193_2_pin3[1]), .pin3(n74193_2_pin3[0]), .pin4(n74193_1_pin13),
    .pin5(n74193_1_pin12), .pin6(n74193_2_pin3[2]), .pin7(n74193_2_pin3[3]), .pin15(D_IN[4]), .pin14(RESET),
    .pin13(n74193_2_pin13), .pin12(n74193_2_pin12), .pin11(n74193_2_pin11), .pin10(D_IN[6]), .pin9(D_IN[7]));
  not not_2 (n74193_2_pin11, LD);
  Hex_Digit_Display hex_digit_display_2 (.value(n74193_2_pin3));  // open: dp
  assign D_OUT[7:4] = EN ? n74193_2_pin3 : 4'bz;  // Controlled_Buffer controlled_buffer_2
  _74193 u_74193_3 (
    .pin1(D_IN[9]), .pin2(n74193_3_pin3[1]), .pin3(n74193_3_pin3[0]), .pin4(n74193_2_pin13),
    .pin5(n74193_2_pin12), .pin6(n74193_3_pin3[2]), .pin7(n74193_3_pin3[3]), .pin15(D_IN[8]), .pin14(RESET),
    .pin13(n74193_3_pin13), .pin12(n74193_3_pin12), .pin11(n74193_3_pin11), .pin10(D_IN[10]), .pin9(D_IN[11]));
  not not_3 (n74193_3_pin11, LD);
  Hex_Digit_Display hex_digit_display_3 (.value(n74193_3_pin3));  // open: dp
  assign D_OUT[11:8] = EN ? n74193_3_pin3 : 4'bz;  // Controlled_Buffer controlled_buffer_3
  _74193 u_74193_4 (
    .pin1(D_IN[13]), .pin2(n74193_4_pin3[1]), .pin3(n74193_4_pin3[0]), .pin4(n74193_3_pin13),
    .pin5(n74193_3_pin12), .pin6(n74193_4_pin3[2]), .pin7(n74193_4_pin3[3]), .pin15(D_IN[12]), .pin14(RESET),
    .pin11(n74193_4_pin11), .pin10(D_IN[14]), .pin9(D_IN[15]));  // open: pin13, pin12
  not not_4 (n74193_4_pin11, LD);
  Hex_Digit_Display hex_digit_display_4 (.value(n74193_4_pin3));  // open: dp
  assign D_OUT[15:12] = EN ? n74193_4_pin3 : 4'bz;  // Controlled_Buffer controlled_buffer_4

  // Other names for the same wires on the sheet: R = RESET
endmodule

module RegisterDriver (
  input  RS0,
  input  RS1,
  input  RS2,
  input  CE,
  input  DEC,
  input  CLC,
  output [1:0] R0,
  output [1:0] R1,
  output [1:0] R2,
  output [1:0] R3,
  output [1:0] R4,
  output [1:0] R5,
  output [1:0] R6,
  output [1:0] R7
);

  wire and_1_out, demultiplexer_1_out0, demultiplexer_1_out1, demultiplexer_2_out0, demultiplexer_2_out1;
  wire [1:0] UP_out;

  Demultiplexer demultiplexer_1 (.out0(demultiplexer_1_out0), .out1(demultiplexer_1_out1), .in(CE), .sel(DEC));
  and and_1 (and_1_out, CE, CLC);
  Demultiplexer demultiplexer_2 (.out0(demultiplexer_2_out0), .out1(demultiplexer_2_out1), .in(and_1_out), .sel(DEC));
  Demultiplexer #(.select(3), .width(2)) demultiplexer_3 (
    .out0(R0), .out1(R1), .out2(R2), .out3(R3), .out4(R4), .out5(R5), .out6(R6), .out7(R7), .in(UP_out),
    .sel({RS2, RS1, RS0}));
  or UP (UP_out[0], demultiplexer_1_out1, demultiplexer_2_out0);
  or DN (UP_out[1], demultiplexer_1_out0, demultiplexer_2_out1);
endmodule
